// Digital circuit 1-bit-half-adder.dig as structural Verilog
module _1_bit_half_adder (
  input  a,
  input  b,
  output sum,
  output cout
);

  wire and_1_out, and_2_out;

  and and_1 (and_1_out, ~a, b);  // And
  and and_2 (and_2_out, a, ~b);  // And
  and and_3 (cout, a, b);
  or or_1 (sum, and_1_out, and_2_out);
endmodule
