// Digital circuit demo.dig as structural Verilog
module demo (
  input  a,
  input  b,
  output \and ,
  output \or ,
  output \xor 
);

  and and_1 (\and , a, b);
  or or_1 (\or , a, b);
  xor xor_1 (\xor , a, b);
endmodule
