// Digital circuit splitter.dig as structural Verilog
module splitter (
  input  [3:0] in_1
);

  _1_bit_half_adder _1_bit_half_adder_1 ();  // open: a, b, sum, cout
  _1_bit_half_adder _1_bit_half_adder_2 ();  // open: a, b, sum, cout
  _1_bit_half_adder _1_bit_half_adder_3 ();  // open: a, b, sum, cout
endmodule
