// Digital circuit demo.dig as structural Verilog
module demo (
  input  a,
  input  b,
  output out_3,
  output out_4,
  output out_5
);

  and and_1 (out_3, a, b);
  or or_1 (out_4, a, b);
  xor xor_1 (out_5, a, b);
endmodule
