// Digital circuit analyze-decode-starter.dig as structural Verilog
module analyze_decode_starter (
  input  [31:0] IW,
  output [2:0] INUM
);

  wire _7_bit_eq_1_eq;

  _7_bit_eq _7_bit_eq_1 (.a(IW[6:0]), .b(7'b0010011), .EQ(_7_bit_eq_1_eq));
  PriorityEncoder #(.Selector_Bits(3)) priorityencoder_1 (
    .in0(_7_bit_eq_1_eq), .num(INUM));  // open: in1, in2, in3, in4, in5, in6, in7, any
endmodule
