// Digital circuit instr-mem-starter.dig as structural Verilog
module instr_mem_starter (
  input  [3:0] A,
  input  PN,
  output [31:0] IW
);

  wire [31:0] rom_1_d;

  ROM #(.AddrBits(4), .Bits(32)) rom_1 (.A(A), .sel(1'b1), .D(rom_1_d));
  Multiplexer #(.Bits(32)) multiplexer_1 (.sel(PN), .in_0(rom_1_d), .in_1(32'h1), .out(IW));

  // Notes on the sheet:
  //   contents of rom_1 (hex, n*v repeats v):
  //   2a502b3,2b282b3,2c50333,628533,d50533,8067,c0001073
endmodule
