// Digital circuit plexers.dig as structural Verilog
module plexers (
  input  [2:0] in_1,
  input  [2:0] in_2,
  input  [2:0] in_3,
  input  [2:0] in_4,
  input  [1:0] sel,
  input  [2:0] sel_2,
  output [2:0] out_5,
  output out_8,
  output out_9,
  output out_10,
  output out_11,
  output out_12,
  output out_13,
  output out_14,
  output out_15
);

  Multiplexer #(.Bits(3), .Selector_Bits(2)) multiplexer_1 (
    .sel(sel), .in_0(in_1), .in_1(in_2), .in_2(in_3), .in_3(in_4), .out(out_5));
  Decoder #(.Selector_Bits(3)) decoder_1 (
    .sel(sel_2), .out_0(out_8), .out_1(out_9), .out_2(out_10), .out_3(out_11), .out_4(out_12),
    .out_5(out_13), .out_6(out_14), .out_7(out_15));

  // Notes on the sheet:
  //   Multiplexer ^^^
  //   <<< Decoder
endmodule
