// Digital circuit 7-bit-eq.dig as structural Verilog
module _7_bit_eq (
  input  [6:0] a,
  input  [6:0] b,
  output EQ
);

  wire _2_bit_eq_1_eq, _2_bit_eq_2_eq, _2_bit_eq_3_eq, xnor_1_out;

  _2_bit_eq _2_bit_eq_1 (.a(a[1:0]), .b(b[1:0]), .EQ(_2_bit_eq_1_eq));
  _2_bit_eq _2_bit_eq_2 (.a(a[3:2]), .b(b[3:2]), .EQ(_2_bit_eq_2_eq));
  _2_bit_eq _2_bit_eq_3 (.a(a[5:4]), .b(b[5:4]), .EQ(_2_bit_eq_3_eq));
  xnor xnor_1 (xnor_1_out, a[6], b[6]);
  and and_1 (EQ, _2_bit_eq_1_eq, _2_bit_eq_2_eq, _2_bit_eq_3_eq, xnor_1_out);
endmodule
