// Digital circuit analyze-decode-starter.dig as structural Verilog
module analyze_decode_starter (
  input  [31:0] IW,
  output [1:0] INUM
);

  wire _7_bit_eq_1_eq, _7_bit_eq_2_eq;

  _7_bit_eq _7_bit_eq_1 (.a(IW[6:0]), .b(7'b0010011), .EQ(_7_bit_eq_1_eq));
  _7_bit_eq _7_bit_eq_2 (.a(IW[6:0]), .b(7'b0110011), .EQ(_7_bit_eq_2_eq));
  PriorityEncoder #(.Selector_Bits(2)) priorityencoder_1 (
    .in0(_7_bit_eq_1_eq), .in1(_7_bit_eq_2_eq), .in2(1'b0), .in3(1'b0), .num(INUM));  // open: any
endmodule
