// Digital circuit plexers.dig as structural Verilog
module plexers (
  input  [2:0] in_1,
  input  [2:0] in_2,
  input  [2:0] in_3,
  input  [2:0] in_4,
  input  [1:0] sel,
  input  [1:0] sel_2,
  output [2:0] out_6,
  output out_7,
  output out_8,
  output out_9,
  output out_10
);

  Multiplexer #(.Bits(3), .Selector_Bits(2)) multiplexer_1 (
    .sel(sel), .in_0(in_1), .in_1(in_3), .in_2(in_4), .in_3(in_2), .out(out_6));
  Decoder #(.Selector_Bits(2)) decoder_1 (.sel(sel_2), .out_0(out_7), .out_1(out_8), .out_2(out_9), .out_3(out_10));

  // Notes on the sheet:
  //   Multiplexer
  //   Decoder
endmodule
