// Digital circuit barrel-shifter.dig as structural Verilog
module barrel_shifter (
  input  [63:0] A,
  input  [6:0] B,
  output [63:0] R
);

  BarrelShifter #(.Bits(64)) barrelshifter_1 (.in(A), .shift(B), .out(R));

  // Notes on the sheet:
  //   sll
endmodule
