// Digital circuit barrel-shifter.dig as structural Verilog
module barrel_shifter (
  input  [63:0] A,
  input  [6:0] B,
  output [63:0] out_3
);

  BarrelShifter #(.Bits(64)) barrelshifter_1 (.in(A), .shift(B), .out(out_3));

  // Other names for the same wires on the sheet: r[63:0] = out_3
endmodule
